# Fritzing sketch 328_term (saved by Fritzing 0.9.1b)
breadboards: 1

parts:
  JP1 = RCA [package=rca_lock]
  U1 = mini DIN 6 Connector [package=mini-din6]  # not connected
  U2 = atmega328 [package=dip]
  U3 = atmega328 [package=dip]
  D1_1N4148 = Diode [package=diode-1n4148]
  D2_1N4148 = Diode [package=diode-1n4148]
  R1 = Resistor [tolerance=±5% resistance=1k package="1206 [SMD]"]
  R2 = Resistor [tolerance=±5% resistance=330 package="1206 [SMD]"]
  XTAL1 = Crystal [frequency="16 Mhz" package=THT]
  C1_-_22pf = Capacitor [package=cap-pth-small2]
  C2_-_22pf = Capacitor [package=cap-pth-small2]
  XTAL2 = Crystal [frequency="16 Mhz" package=THT]
  C3_-_22pf1 = Capacitor [package=cap-pth-small2]
  C4_-_22pf1 = Capacitor [package=cap-pth-small2]
  IC1 = Voltage Regulator [package=to220-igo]
  C1 = Ceramic Capacitor [capacitance=100nF package="100 mil [THT, multilayer]"]
  C2 = Ceramic Capacitor [capacitance=100nF package="100 mil [THT, multilayer]"]
  C3 = Ceramic Capacitor [capacitance=100nF package="100 mil [THT, multilayer]"]
  C4 = Ceramic Capacitor [capacitance=100nF package="100 mil [THT, multilayer]"]
  C5 = Capacitor Polarized [package=cpol-radial-10uf-25v]
  C6 = Capacitor Polarized [package=cpol-radial-10uf-25v]

nets:
  N1: JP1.PIN, R1.Pin_1, R2.Pin_1
  GND: JP1.SHELL, U2.GND, U3.GND#21, C1_-_22pf.2, C2_-_22pf.2, C3_-_22pf1.2, C4_-_22pf1.2, IC1.GND, C1.1, C3.0, C4.1, C5.-, C6.-
  N2: U2.D0_(RX), U3.D1_(TX)
  N3: U2.D1_(TX), U3.D0_(RX)
  N4: U2.VCC, C3.1
  N5: U2.XLAT1, XTAL2.pin_1, C3_-_22pf1.1
  N6: U2.XLAT2, XTAL2.pin_0, C4_-_22pf1.1
  5V: U2.AVCC, U3.VCC, U3.AVCC, IC1.IN, C1.0, C2.1, C4.0, C6.+
  N7: U3.GND#7, C2.0
  N8: U3.XLAT1, XTAL1.pin_1, C2_-_22pf.1
  N9: U3.XLAT2, XTAL1.pin_0, C1_-_22pf.1
  N10: U3.D9_(PWM), D1_1N4148.A
  N11: U3.D11_(PWM), D2_1N4148.A
  N12: D1_1N4148.C, R1.Pin_0
  N13: D2_1N4148.C, R2.Pin_0
  N14: IC1.OUT, C5.+

notes:
  sig_pixel
  sig_sync
  data
  irq
